# Fritzing sketch Laurel (saved by Fritzing 0.9.9b)
breadboards: 1

parts:
  Part1 = Adafruit Feather nRF52 [part_number="Adafruit #3406"]
  Part2 = Adafruit OLED FeatherWing [part_number="Adafruit #2900"]
  R1 = Resistor [tolerance=±5% resistance=10000 package="0603 [SMD]"]
  P1 = Multimeter straight black probe
  P2 = Multimeter straight red probe
  Part4 = Soil Moisture Sensor
  Q1 = NPN-Transistor [package="TO92 [THT]"]
  R2 = Resistor [tolerance=±5% resistance=220 package="0603 [SMD]"]
  M1 = DC Motor
  D1 = Diode [package=diode-1n4001]

nets:
  3.3V: Part1.3.3V, P2.Probe_tip, P2.Probe_meter_end, Part4.VCC
  GND: Part1.GND, R1.Pin_1, Part4.GND, M1.pin_1
  N1: Part1.A3/0.05, R1.Pin_0, P1.Probe_tip
  N2: Part1.A5/0.29, Part4.SIG
  N3: Part1.SDA, Part2.SDA
  N4: Part1.SCL, Part2.SCL
  N5: Part1.P0.27, Part2.H
  N6: Part1.A6/P0.30, Part2.I
  N7: Part1.A7/P0.31, Part2.J
  N8: Part1.P0.07, R2.Pin_1
  N9: Part1.VBAT, Q1.C, D1.C
  N10: Q1.E, M1.pin_2
  N11: Q1.B, R2.Pin_0

custom parts:
  Adafruit OLED FeatherWing: This is the FeatherWing OLED: it adds a 128x32 monochrome OLED plus 3 user buttons to any Feather main board. These displays are small, only about 1" diagonal, but very readable due to the high contrast of an OLED display. This screen is made of 128x32 individual white OLED pixels and because the display makes its own light, no backlight is required. This reduces the power required to run the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
